# Fritzing sketch LCD_Wiring_Matrix_Display (saved by Fritzing 0.9.6b)
breadboards: 2

parts:
  RPi1 = Raspberry Pi 4B
  Q1 = NPN-Transistor [package="TO92 [THT]"]
  Q2 = PNP-Transistor [package="TO92 [THT]"]
  R2 = Resistor [tolerance=±5% power=0.25 resistance=10k package=THT]
  R3 = Resistor [tolerance=±5% power=0.25 resistance=1.2k package=THT]
  R4 = Resistor [tolerance=±5% power=0.25 resistance=10k package=THT]
  GLCD_128x1 = 128 x 64 Graphic LCD
  J1 = JST-03JQ-BT [part_number=JST-JQ-BT package=THT]
  J2 = JST-03JQ-BT [part_number=JST-JQ-BT package=THT]
  R5 = resistor-upright [tolerance=±5% resistance=1.2k]
  R1 = TRIMPOT [package=trimpot_pth_s3_lock]
  S1 = Square Pushbutton

nets:
  N1: RPi1.GPIO2, GLCD_128x1.4_D/I
  N2: RPi1.5V, Q2.E, R2.Pin_0, GLCD_128x1.2_Vdd, J1.pin2, R1.CW, S1.leg1
  N3: RPi1.GPIO3, GLCD_128x1.5_R/W
  N4: RPi1.GND, Q1.E, R4.Pin_0, GLCD_128x1.1_Vss, GLCD_128x1.18_Vout, GLCD_128x1.20_K(-), J1.pin1, J2.pin2, R1.CCW
  N5: RPi1.GPIO4, GLCD_128x1.6_Enable
  N6: RPi1.GPIO14, GLCD_128x1.15_CS1
  N7: RPi1.GPIO15, GLCD_128x1.16_CS2
  N8: RPi1.GPIO17, R5.connector0
  N9: RPi1.GPIO18, GLCD_128x1.17_RST
  N10: RPi1.GPIO27, S1.leg0
  N11: RPi1.GPIO25, GLCD_128x1.7_DB0
  N12: RPi1.GPIO8, GLCD_128x1.8_DB1
  N13: RPi1.GPIO7, GLCD_128x1.9_BD2
  N14: RPi1.ID_SD, GLCD_128x1.11_DB4
  N15: RPi1.ID_SC, GLCD_128x1.10_DB3
  N16: RPi1.GPIO5, GLCD_128x1.12_DB5
  N17: RPi1.GPIO6, GLCD_128x1.13_DB6
  N18: RPi1.GPIO13, GLCD_128x1.14_DB7
  N19: Q1.B, R4.Pin_1, R5.connector1
  N20: Q1.C, R2.Pin_1, R3.Pin_0
  N21: Q2.B, R3.Pin_1
  N22: Q2.C, GLCD_128x1.19_A(+), J2.pin1
  N23: GLCD_128x1.3_Vo, J1.pin3, R1.WIPER
